// Logisim project Processor.circ as structural Verilog
module Processor (
  input  Reset,
  input  [3:0] Display_Address
);

  wire alu_1_is, alu_1_is_2, Clock, control_unit_1_isimmediate, ex_ma_latch_1_out_14, ex_ma_latch_1_out_15,
       ex_ma_latch_1_out_16, flags_1_flags_e, flags_1_flags_gt, isBranchTaken, isWB, isWb_t,
       of_ex_latch_1_p14, of_ex_latch_1_p15, of_ex_latch_1_p18, of_ex_latch_1_p19, of_ex_latch_1_p20,
       of_ex_latch_1_p21, of_ex_latch_1_p22, of_ex_latch_1_p23, of_ex_latch_1_p24, of_ex_latch_1_p25,
       of_ex_latch_1_p26, of_ex_latch_1_p27, of_ex_latch_1_p28, of_ex_latch_1_p29, of_ex_latch_1_p30,
       of_ex_latch_1_p31;
  wire [1:0] ma_rw_latch_1_p10;
  wire [3:0] if_of_latch_1_out_7_2, if_of_latch_1_out_7_3, multiplexer_5_out, multiplexer_6_out,
       multiplexer_7_out, register_file_1_displayd_2, register_file_1_displayd_3;
  wire [12:0] of_ex_latch_1_p16, of_ex_latch_1_p17;
  wire [23:0] register_file_1_displayd;
  wire [31:0] adder_1_out, alu_1_aluresult, bit_extender_1_out, branchTarget, calculate_immediate_1_immx,
       data, ex_ma_latch_1_out_10, ex_ma_latch_1_out_11, ex_ma_latch_1_out_12, ex_ma_latch_1_out_13,
       if_of_latch_1_out_6, if_of_latch_1_out_7, ma_rw_latch_1_p3, ma_rw_latch_1_p5, ma_rw_latch_1_p6,
       ma_rw_latch_1_p7, multiplexer_1_out, of_ex_latch_1_p3, of_ex_latch_1_p4, of_ex_latch_1_p5,
       of_ex_latch_1_p6, of_ex_latch_1_p8, of_ex_latch_1_p10, of_ex_latch_1_p13, rom_1_data, shifter_1_out;

  IF_OF_Latch if_of_latch_1 (
    .in_3(Clock), .in_1(if_of_latch_1_out_6), .in_2(rom_1_data), .out_6(if_of_latch_1_out_6),
    .out_7({if_of_latch_1_out_7[31:26], if_of_latch_1_out_7_3, if_of_latch_1_out_7_2, if_of_latch_1_out_7[17:0]}),
    .in_4(Clock));  // open: out_5
  // OF_EX_Latch of_ex_latch_1: pin names not known; wires that end beside it: Clock, if_of_latch_1_out_6, of_ex_latch_1_p3, of_ex_latch_1_p4, of_ex_latch_1_p5, of_ex_latch_1_p6, of_ex_latch_1_p5, of_ex_latch_1_p8, of_ex_latch_1_p5, of_ex_latch_1_p10, of_ex_latch_1_p5, {if_of_latch_1_out_7[31:26], if_of_latch_1_out_7_3, if_of_latch_1_out_7_2, if_of_latch_1_out_7[17:0]}, of_ex_latch_1_p13, of_ex_latch_1_p14, of_ex_latch_1_p15, of_ex_latch_1_p16, of_ex_latch_1_p17, of_ex_latch_1_p18, of_ex_latch_1_p19, of_ex_latch_1_p20, of_ex_latch_1_p21, of_ex_latch_1_p22, of_ex_latch_1_p23, of_ex_latch_1_p24, of_ex_latch_1_p25, of_ex_latch_1_p26, of_ex_latch_1_p27, of_ex_latch_1_p28, of_ex_latch_1_p29, of_ex_latch_1_p30, of_ex_latch_1_p31
  EX_MA_Latch ex_ma_latch_1 (
    .in_9(Clock), .in_5(of_ex_latch_1_p3), .in_6(alu_1_aluresult), .in_7(of_ex_latch_1_p5),
    .in_8(of_ex_latch_1_p13), .isLd(of_ex_latch_1_p25), .isSt(of_ex_latch_1_p27), .isCall(of_ex_latch_1_p29),
    .isWb(of_ex_latch_1_p31), .out_10(ex_ma_latch_1_out_10), .out_11(ex_ma_latch_1_out_11),
    .out_12(ex_ma_latch_1_out_12), .out_13(ex_ma_latch_1_out_13), .out_14(ex_ma_latch_1_out_14),
    .out_15(ex_ma_latch_1_out_15), .out_16(ex_ma_latch_1_out_16), .out_17(of_ex_latch_1_p31));
  // MA_RW_Latch ma_rw_latch_1: pin names not known; wires that end beside it: Clock, ex_ma_latch_1_out_10, ma_rw_latch_1_p3, ex_ma_latch_1_out_11, ma_rw_latch_1_p5, ma_rw_latch_1_p6, ma_rw_latch_1_p7, ex_ma_latch_1_out_13, ex_ma_latch_1_out_14, ma_rw_latch_1_p10[0], ex_ma_latch_1_out_16, ma_rw_latch_1_p10[1], of_ex_latch_1_p31, isWB
  Register #(.width(32), .trigger("falling")) PC (
    .D(multiplexer_1_out), .Q(if_of_latch_1_out_6), .clk(Clock), .clr(Reset));  // open: en
  Multiplexer #(.width(32), .enable("false")) multiplexer_1 (
    .in0(adder_1_out), .in1(branchTarget), .out(multiplexer_1_out), .sel(isBranchTaken));
  assign bit_extender_1_out = {{5{if_of_latch_1_out_7[26]}}, {if_of_latch_1_out_7[26], if_of_latch_1_out_7_3, if_of_latch_1_out_7_2, if_of_latch_1_out_7[17:0]}};  // Bit_Extender bit_extender_1
  Adder #(.width(32)) adder_1 (.a(32'h4), .b(if_of_latch_1_out_6), .out(adder_1_out));  // open: cin, cout
  Shifter #(.width(32)) shifter_1 (.in(bit_extender_1_out), .\dist (5'b00010), .out(shifter_1_out));
  ALU alu_1 (
    .A(of_ex_latch_1_p5), .B(of_ex_latch_1_p5), .ALUsignals(of_ex_latch_1_p17), .aluResult(alu_1_aluresult),
    .is(alu_1_is), .is_2(alu_1_is_2));
  Adder #(.width(32)) adder_2 (.a(ma_rw_latch_1_p3), .b(32'h4), .out(ma_rw_latch_1_p7));  // open: cin, cout
  Calculate_Immediate calculate_immediate_1 (.imm(if_of_latch_1_out_7[17:0]), .immx(calculate_immediate_1_immx));
  Adder #(.width(32)) adder_3 (.a(shifter_1_out), .b(if_of_latch_1_out_6), .out(of_ex_latch_1_p4));  // open: cin, cout
  Multiplexer #(.width(32), .enable("false")) multiplexer_2 (
    .in0(of_ex_latch_1_p5), .in1(of_ex_latch_1_p5), .out(branchTarget), .sel(of_ex_latch_1_p15));
  Multiplexer #(.select(2), .width(32), .enable("false")) multiplexer_3 (
    .in0(ma_rw_latch_1_p5), .in1(ma_rw_latch_1_p7), .in2(ma_rw_latch_1_p7), .out(data),
    .sel(ma_rw_latch_1_p10));  // open: in3
  Clock u_Clock (.out(Clock));
  ROM #(.addrWidth(24), .dataWidth(32)) rom_1 (.addr(if_of_latch_1_out_6[25:2]), .data(rom_1_data));  // open: sel
  Multiplexer #(.width(32), .enable("false")) multiplexer_4 (
    .in0(of_ex_latch_1_p10), .in1(calculate_immediate_1_immx), .out(of_ex_latch_1_p6),
    .sel(control_unit_1_isimmediate));
  Flags flags_1 (
    .isCmp(of_ex_latch_1_p17[0]), .is(alu_1_is), .is_2(alu_1_is_2), .flags_GT(flags_1_flags_gt),
    .flags_E(flags_1_flags_e));
  Memory_Unit memory_unit_1 (
    .MAR(ex_ma_latch_1_out_11), .ldResult(ma_rw_latch_1_p6), .MDR(ex_ma_latch_1_out_12),
    .isSt(ex_ma_latch_1_out_15), .isLd(ex_ma_latch_1_out_14), .Clock(Clock), .Reset(Reset));
  Hex_Digit_Display hex_digit_display_1 (.value(register_file_1_displayd_3));  // open: dp
  Multiplexer #(.width(4), .enable("false")) multiplexer_5 (
    .in0(if_of_latch_1_out_7[17:14]), .in1(if_of_latch_1_out_7_3), .out(multiplexer_5_out),
    .sel(of_ex_latch_1_p26));
  Hex_Digit_Display hex_digit_display_2 (.value(register_file_1_displayd_2));  // open: dp
  Multiplexer #(.width(4), .enable("false")) multiplexer_6 (
    .in0(if_of_latch_1_out_7_2), .in1(4'b1111), .out(multiplexer_6_out), .sel(of_ex_latch_1_p14));
  Register_File register_file_1 (
    .ReadA1(multiplexer_6_out), .ReadA2(multiplexer_5_out), .WriteE(isWb_t), .WriteD(data),
    .ReadD1(of_ex_latch_1_p8), .ReadD2(of_ex_latch_1_p10), .Clock(Clock), .Reset(Reset),
    .DisplayD({register_file_1_displayd_3, register_file_1_displayd_2, register_file_1_displayd}),
    .DisplayA(Display_Address), .WriteA(multiplexer_7_out));
  Branch_Unit branch_unit_1 (
    .isBeq(of_ex_latch_1_p19), .isUBranch(of_ex_latch_1_p23), .flags_E(flags_1_flags_e),
    .isBgt(of_ex_latch_1_p21), .flags_GT(flags_1_flags_gt), .isBranchTaken(isBranchTaken));
  Hex_Digit_Display hex_digit_display_3 (.value(register_file_1_displayd[23:20]));  // open: dp
  Hex_Digit_Display hex_digit_display_4 (.value(register_file_1_displayd[15:12]));  // open: dp
  Hex_Digit_Display hex_digit_display_5 (.value(register_file_1_displayd[19:16]));  // open: dp
  Control_Unit control_unit_1 (
    .isSt(of_ex_latch_1_p26), .isLd(of_ex_latch_1_p24), .isBeq(of_ex_latch_1_p18), .isBgt(of_ex_latch_1_p20),
    .isRet(of_ex_latch_1_p14), .I_bit(if_of_latch_1_out_7[26]), .isImmediate(control_unit_1_isimmediate),
    .opcode(if_of_latch_1_out_7[31:27]), .isWb(of_ex_latch_1_p30), .isUbranch(of_ex_latch_1_p22),
    .isCall(of_ex_latch_1_p28), .ALUsignals(of_ex_latch_1_p16));
  Hex_Digit_Display hex_digit_display_6 (.value(register_file_1_displayd[11:8]));  // open: dp
  Hex_Digit_Display hex_digit_display_7 (.value(register_file_1_displayd[7:4]));  // open: dp
  Multiplexer #(.width(4), .enable("false")) multiplexer_7 (
    .in0(if_of_latch_1_out_7_3), .in1(4'b1111), .out(multiplexer_7_out), .sel(of_ex_latch_1_p28));
  Hex_Digit_Display hex_digit_display_8 (.value(register_file_1_displayd[3:0]));  // open: dp

  // Notes on the sheet:
  //   ALUsignals
  //   B
  //   pc
  //   pc+4
  //   branchTarget
  //   offset
  //   pc
  //   branchTarget
  //   A
  //   ALU
  //   aluResult
  //   MAR
  //   Instruction Memory
  //   calc immx
  //   imm
  //   isRet
  //   is>
  //   is=
  //   MDR
  //   Memory
  //   Unit
  //   ldResult
  //   data
  //   SINGLE CYCLE PROCESSOR
  //   contents of rom_1 (hex, n*v repeats v):
  //   4c00000a 98000002 90000000 2c000001 88000003 4c400001 a0000000 fb80008 7c380000 7ff80004 c000001
  //   9ffffff8 77f80004 74380000 7b80008 10404000 a0000000
  //   immx
  //   Flags
  //   isCmp
  //   isLd
  //   isSt
  //   isLd
  //   isCall
  //   rs2
  //   rd
  //   isSt
  //   Register
  //   File
  //   op2
  //   isImmediate
  //   flags(GT)
  //   flags(E)
  //   instruction
  //   isRet
  //   E
  //   A
  //   data
  //   address
  //   D
  //   op1
  //   Branch
  //   Unit
  //   opcode
  //   I bit
  //   isWb
  //   isBeq
  //   isBgt
  //   isUBranch
  //   Display Register
  //   CONTROL
  //   UNIT
  //   isCall
  //   rd
endmodule

module Control_Unit (
  input  I_bit,
  input  [4:0] opcode,
  output isSt,
  output isLd,
  output isBeq,
  output isBgt,
  output isRet,
  output isImmediate,
  output isWb,
  output isUbranch,
  output isCall,
  output [12:0] ALUsignals
);

  wire and_6_out, and_7_out, and_8_out, and_9_out, and_10_out, and_12_out, and_13_out, nand_1_out;

  nand nand_1 (nand_1_out, opcode[0], opcode[1]);
  and and_1 (isSt, opcode[0], opcode[1], opcode[2], opcode[3], ~opcode[4]);  // AND_Gate
  and and_2 (isLd, ~opcode[0], opcode[1], opcode[2], opcode[3], ~opcode[4]);  // AND_Gate
  and and_3 (isBeq, ~opcode[0], ~opcode[1], ~opcode[2], ~opcode[3], opcode[4]);  // AND_Gate
  and and_4 (isBgt, opcode[0], ~opcode[1], ~opcode[2], ~opcode[3], opcode[4]);  // AND_Gate
  and and_5 (isRet, ~opcode[0], ~opcode[1], opcode[2], ~opcode[3], opcode[4]);  // AND_Gate
  and and_6 (and_6_out, opcode[0], ~opcode[1], opcode[2], ~opcode[4]);  // AND_Gate
  and and_7 (and_7_out, opcode[0], opcode[2], opcode[3], ~opcode[4]);  // AND_Gate
  and and_8 (and_8_out, opcode[4], nand_1_out);
  and and_9 (and_9_out, opcode[1], ~opcode[2], ~opcode[3], opcode[4]);  // AND_Gate
  and and_10 (and_10_out, ~opcode[0], ~opcode[1], opcode[2], ~opcode[3], opcode[4]);  // AND_Gate
  and and_11 (isCall, opcode[0], opcode[1], ~opcode[2], ~opcode[3], opcode[4]);  // AND_Gate
  and and_12 (and_12_out, ~opcode[0], ~opcode[1], ~opcode[2], ~opcode[3], ~opcode[4]);  // AND_Gate
  and and_13 (and_13_out, opcode[1], opcode[2], opcode[3], ~opcode[4]);  // AND_Gate
  and isSub (ALUsignals[2], opcode[0], ~opcode[1], ~opcode[2], ~opcode[3], ~opcode[4]);  // AND_Gate
  and isCmp (ALUsignals[0], opcode[0], ~opcode[1], opcode[2], ~opcode[3], ~opcode[4]);  // AND_Gate
  and isMul (ALUsignals[3], ~opcode[0], opcode[1], ~opcode[2], ~opcode[3], ~opcode[4]);  // AND_Gate
  and isDiv (ALUsignals[4], opcode[0], opcode[1], ~opcode[2], ~opcode[3], ~opcode[4]);  // AND_Gate
  and isMod (ALUsignals[5], ~opcode[0], ~opcode[1], opcode[2], ~opcode[3], ~opcode[4]);  // AND_Gate
  and isLsl (ALUsignals[7], ~opcode[0], opcode[1], ~opcode[2], opcode[3], ~opcode[4]);  // AND_Gate
  and isLsr (ALUsignals[8], opcode[0], opcode[1], ~opcode[2], opcode[3], ~opcode[4]);  // AND_Gate
  and isAsr (ALUsignals[9], ~opcode[0], ~opcode[1], opcode[2], opcode[3], ~opcode[4]);  // AND_Gate
  and isOr (ALUsignals[12], opcode[0], opcode[1], opcode[2], ~opcode[3], ~opcode[4]);  // AND_Gate
  and isAnd (ALUsignals[11], ~opcode[0], opcode[1], opcode[2], ~opcode[3], ~opcode[4]);  // AND_Gate
  and isNot (ALUsignals[10], ~opcode[0], ~opcode[1], ~opcode[2], opcode[3], ~opcode[4]);  // AND_Gate
  and isMov (ALUsignals[6], opcode[0], ~opcode[1], ~opcode[2], opcode[3], ~opcode[4]);  // AND_Gate
  or or_1 (isUbranch, and_9_out, and_10_out);
  or isAdd (ALUsignals[1], and_12_out, and_13_out);
  nor nor_1 (isWb, and_6_out, and_7_out, and_8_out);

  assign isImmediate = I_bit;

  // Notes on the sheet:
  //   op1
  //   op2
  //   op3
  //   op4
  //   op5
endmodule

module Register_File (
  input  Clock,
  input  Reset,
  input  [31:0] WriteD,
  input  [3:0] ReadA1,
  input  WriteE,
  input  [3:0] WriteA,
  input  [3:0] ReadA2,
  input  [3:0] DisplayA,
  output [31:0] ReadD1,
  output [31:0] ReadD2,
  output [31:0] DisplayD
);

  wire demultiplexer_1_out0, demultiplexer_1_out1, demultiplexer_1_out2, demultiplexer_1_out3,
       demultiplexer_1_out4, demultiplexer_1_out5, demultiplexer_1_out6, demultiplexer_1_out7,
       demultiplexer_1_out8, demultiplexer_1_out9, demultiplexer_1_out10, demultiplexer_1_out11,
       demultiplexer_1_out12, demultiplexer_1_out13, demultiplexer_1_out14, demultiplexer_1_out15,
       multiplexer_2_out, or_1_out, or_2_out;
  wire [31:0] multiplexer_1_out, r0_q, r1_q, r2_q, r3_q, r4_q, r5_q, r6_q, r7_q, r8_q, r9_q, r10_q, r11_q,
       r12_q, r13_q, r14_q, r15_q;

  Demultiplexer #(.select(4), .disabled(0), .enable("false")) demultiplexer_1 (
    .out0(demultiplexer_1_out0), .out1(demultiplexer_1_out1), .out2(demultiplexer_1_out2),
    .out3(demultiplexer_1_out3), .out4(demultiplexer_1_out4), .out5(demultiplexer_1_out5),
    .out6(demultiplexer_1_out6), .out7(demultiplexer_1_out7), .out8(demultiplexer_1_out8),
    .out9(demultiplexer_1_out9), .out10(demultiplexer_1_out10), .out11(demultiplexer_1_out11),
    .out12(demultiplexer_1_out12), .out13(demultiplexer_1_out13), .out14(demultiplexer_1_out14),
    .out15(demultiplexer_1_out15), .in(WriteE), .sel(WriteA));
  Multiplexer #(.width(32), .enable("false")) multiplexer_1 (
    .in0(WriteD), .in1(32'h3fffffc), .out(multiplexer_1_out), .sel(Reset));
  or or_1 (or_1_out, demultiplexer_1_out14, Reset);
  Multiplexer #(.enable("false")) multiplexer_2 (.in0(or_2_out), .out(multiplexer_2_out), .sel(1'b0));  // open: in1
  or or_2 (or_2_out, Clock, Reset);
  Register #(.width(32)) r0 (.D(WriteD), .en(demultiplexer_1_out0), .Q(r0_q), .clk(Clock), .clr(Reset));
  Register #(.width(32)) r1 (.D(WriteD), .en(demultiplexer_1_out1), .Q(r1_q), .clk(Clock), .clr(Reset));
  Register #(.width(32)) r2 (.D(WriteD), .en(demultiplexer_1_out2), .Q(r2_q), .clk(Clock), .clr(Reset));
  Register #(.width(32)) r3 (.D(WriteD), .en(demultiplexer_1_out3), .Q(r3_q), .clk(Clock), .clr(Reset));
  Register #(.width(32)) r4 (.D(WriteD), .en(demultiplexer_1_out4), .Q(r4_q), .clk(Clock), .clr(Reset));
  Register #(.width(32)) r5 (.D(WriteD), .en(demultiplexer_1_out5), .Q(r5_q), .clk(Clock), .clr(Reset));
  Register #(.width(32)) r6 (.D(WriteD), .en(demultiplexer_1_out6), .Q(r6_q), .clk(Clock), .clr(Reset));
  Register #(.width(32)) r7 (.D(WriteD), .en(demultiplexer_1_out7), .Q(r7_q), .clk(Clock), .clr(Reset));
  Register #(.width(32)) r8 (.D(WriteD), .en(demultiplexer_1_out8), .Q(r8_q), .clk(Clock), .clr(Reset));
  Register #(.width(32)) r9 (.D(WriteD), .en(demultiplexer_1_out9), .Q(r9_q), .clk(Clock), .clr(Reset));
  Register #(.width(32)) r10 (.D(WriteD), .en(demultiplexer_1_out10), .Q(r10_q), .clk(Clock), .clr(Reset));
  Register #(.width(32)) r11 (.D(WriteD), .en(demultiplexer_1_out11), .Q(r11_q), .clk(Clock), .clr(Reset));
  Register #(.width(32)) r12 (.D(WriteD), .en(demultiplexer_1_out12), .Q(r12_q), .clk(Clock), .clr(Reset));
  Register #(.width(32)) r13 (.D(WriteD), .en(demultiplexer_1_out13), .Q(r13_q), .clk(Clock), .clr(Reset));
  Register #(.width(32)) r14 (.D(multiplexer_1_out), .en(or_1_out), .Q(r14_q), .clk(multiplexer_2_out));  // open: clr
  Register #(.width(32)) r15 (.D(WriteD), .en(demultiplexer_1_out15), .Q(r15_q), .clk(Clock), .clr(Reset));
  Multiplexer #(.select(4), .width(32), .disabled(0), .enable("false")) multiplexer_3 (
    .in0(r0_q), .in1(r1_q), .in2(r2_q), .in3(r3_q), .in4(r4_q), .in5(r5_q), .in6(r6_q), .in7(r7_q),
    .in8(r8_q), .in9(r9_q), .in10(r10_q), .in11(r11_q), .in12(r12_q), .in13(r13_q), .in14(r14_q),
    .in15(r15_q), .out(ReadD1), .sel(ReadA1));
  Multiplexer #(.select(4), .width(32), .disabled(0), .enable("false")) multiplexer_4 (
    .in0(r0_q), .in1(r1_q), .in2(r2_q), .in3(r3_q), .in4(r4_q), .in5(r5_q), .in6(r6_q), .in7(r7_q),
    .in8(r8_q), .in9(r9_q), .in10(r10_q), .in11(r11_q), .in12(r12_q), .in13(r13_q), .in14(r14_q),
    .in15(r15_q), .out(ReadD2), .sel(ReadA2));
  Multiplexer #(.select(4), .width(32), .disabled(0), .enable("false")) multiplexer_5 (
    .in0(r0_q), .in1(r1_q), .in2(r2_q), .in3(r3_q), .in4(r4_q), .in5(r5_q), .in6(r6_q), .in7(r7_q),
    .in8(r8_q), .in9(r9_q), .in10(r10_q), .in11(r11_q), .in12(r12_q), .in13(r13_q), .in14(r14_q),
    .in15(r15_q), .out(DisplayD), .sel(DisplayA));
endmodule

module ALU (
  input  [31:0] A,
  input  [31:0] B,
  input  [12:0] ALUsignals,
  output [31:0] aluResult,
  output is,
  output is_2
);

  wire [31:0] adder_1_out, and_1_out, divider_1_out, divider_1_rem, multiplier_1_out, not_1_out, or_1_out,
       shifter_1_out, shifter_2_out, shifter_3_out, subtractor_1_out;

  Adder #(.width(32)) adder_1 (.a(A), .b(B), .out(adder_1_out));  // open: cin, cout
  Subtractor #(.width(32)) subtractor_1 (.a(A), .b(B), .out(subtractor_1_out));  // open: bin, bout
  Multiplier #(.width(32)) multiplier_1 (.a(A), .b(B), .out(multiplier_1_out));  // open: cin, cout
  Divider #(.width(32)) divider_1 (.a(A), .b(B), .out(divider_1_out), .rem(divider_1_rem));  // open: upper
  Comparator #(.width(32)) comparator_1 (.a(A), .b(B), .gt(is), .eq(is_2));  // open: lt
  Shifter #(.width(32)) shifter_1 (.in(A), .\dist (B[4:0]), .out(shifter_1_out));
  Shifter #(.width(32), .shift("lr")) shifter_2 (.in(A), .\dist (B[4:0]), .out(shifter_2_out));
  Shifter #(.width(32), .shift("ar")) shifter_3 (.in(A), .\dist (B[4:0]), .out(shifter_3_out));
  assign not_1_out = ~B;  // NOT_Gate not_1, 32 bits wide
  assign and_1_out = A & B;  // AND_Gate and_1, 32 bits wide
  assign or_1_out = A | B;  // OR_Gate or_1, 32 bits wide
  assign aluResult = ALUsignals[1] ? adder_1_out : 32'bz;  // Controlled_Buffer controlled_buffer_1
  assign aluResult = ALUsignals[2] ? subtractor_1_out : 32'bz;  // Controlled_Buffer controlled_buffer_2
  assign aluResult = ALUsignals[3] ? multiplier_1_out : 32'bz;  // Controlled_Buffer controlled_buffer_3
  assign aluResult = ALUsignals[4] ? divider_1_out : 32'bz;  // Controlled_Buffer controlled_buffer_4
  assign aluResult = ALUsignals[5] ? divider_1_rem : 32'bz;  // Controlled_Buffer controlled_buffer_5
  assign aluResult = ALUsignals[6] ? B : 32'bz;  // Controlled_Buffer controlled_buffer_6
  assign aluResult = ALUsignals[7] ? shifter_1_out : 32'bz;  // Controlled_Buffer controlled_buffer_7
  assign aluResult = ALUsignals[8] ? shifter_2_out : 32'bz;  // Controlled_Buffer controlled_buffer_8
  assign aluResult = ALUsignals[9] ? shifter_3_out : 32'bz;  // Controlled_Buffer controlled_buffer_9
  assign aluResult = ALUsignals[10] ? not_1_out : 32'bz;  // Controlled_Buffer controlled_buffer_10
  assign aluResult = ALUsignals[11] ? and_1_out : 32'bz;  // Controlled_Buffer controlled_buffer_11
  assign aluResult = ALUsignals[12] ? or_1_out : 32'bz;  // Controlled_Buffer controlled_buffer_12

  // Notes on the sheet:
  //   add
  //   sub
  //   mul
  //   div
  //   cmp
  //   lsr
  //   mod
  //   lsl
  //   asr
endmodule

module Flags (
  input  isCmp,
  input  is,
  input  is_2,
  output flags_GT,
  output flags_E
);

  D_Flip_Flop #(.trigger("high")) d_ff_1 (.clk(isCmp), .D(is), .Q(flags_GT));  // open: Qn, preset, en, reset
  D_Flip_Flop #(.trigger("high")) d_ff_2 (.clk(isCmp), .D(is_2), .Q(flags_E));  // open: Qn, preset, en, reset
endmodule

module Branch_Unit (
  input  isUBranch,
  input  isBeq,
  input  flags_E,
  input  isBgt,
  input  flags_GT,
  output isBranchTaken
);

  wire and_1_out, and_2_out;

  and and_1 (and_1_out, isBeq, flags_E);
  and and_2 (and_2_out, isBgt, flags_GT);
  or or_1 (isBranchTaken, isUBranch, and_1_out, and_2_out);
endmodule

module Memory_Unit (
  input  [31:0] MAR,
  input  isLd,
  input  [31:0] MDR,
  input  isSt,
  input  Clock,
  input  Reset,
  output [31:0] ldResult
);

  RAM #(.addrWidth(24), .dataWidth(32), .bus("separate")) ram_1 (
    .addr(MAR[25:2]), .din(MDR), .data(ldResult), .str(isSt), .clk(Clock), .ld(isLd), .clr(Reset));  // open: sel
endmodule

module Calculate_Immediate (
  input  [17:0] imm,
  output [31:0] immx
);

  wire [31:0] bit_extender_1_out, bit_extender_2_out, shifter_1_out;

  assign bit_extender_1_out = {{16{1'b0}}, imm[15:0]};  // Bit_Extender bit_extender_1
  assign bit_extender_2_out = {{16{imm[15]}}, imm[15:0]};  // Bit_Extender bit_extender_2
  Shifter #(.width(32)) shifter_1 (.in(bit_extender_1_out), .\dist (5'b10000), .out(shifter_1_out));
  Multiplexer #(.select(2), .width(32), .enable("false")) multiplexer_1 (
    .in0(bit_extender_2_out), .in1(bit_extender_1_out), .in2(shifter_1_out), .out(immx), .sel(imm[17:16]));  // open: in3

  // Notes on the sheet:
  //   modifier bits
  //   high
  //   default
  //   unsigned
endmodule

module IF_OF_Latch (
  input  [31:0] in_1,
  input  [31:0] in_2,
  input  in_3,
  input  in_4,
  output [31:0] out_5,
  output [31:0] out_6,
  output [31:0] out_7
);

  Register #(.width(32)) register_1 (.D(in_1), .Q(out_6), .clk(in_3), .clr(in_4));  // open: en
  Register #(.width(32)) register_2 (.D(in_2), .Q(out_5), .clk(in_3), .clr(in_4));  // open: en

  assign out_7 = out_5;
endmodule

module OF_EX_Latch (
  input  in_1,
  input  [12:0] in_2,
  input  [31:0] in_3,
  input  [31:0] in_4,
  input  [31:0] in_5,
  input  [31:0] in_6,
  input  [31:0] in_7,
  input  [31:0] isRet,
  input  in_9,
  input  isBgt,
  input  isUBranch,
  input  isLd,
  input  isSt,
  input  in_14,
  input  in_15,
  input  in_16,
  output [31:0] out_17,
  output [31:0] out_18,
  output [31:0] out_19,
  output [31:0] out_20,
  output [31:0] out_21,
  output [31:0] out_22,
  output [12:0] out_23,
  output out_24,
  output out_25,
  output out_26,
  output out_27,
  output out_28,
  output out_29,
  output out_30,
  output out_31
);

  Register #(.width(32)) register_1 (.D(in_3), .Q(out_17), .clk(in_16));  // open: en, clr
  Register #(.width(32)) register_2 (.D(in_4), .Q(out_18), .clk(in_16));  // open: en, clr
  Register #(.width(32)) register_3 (.D(in_5), .Q(out_19), .clk(in_16));  // open: en, clr
  Register #(.width(32)) register_4 (.D(in_6), .Q(out_20), .clk(in_16));  // open: en, clr
  Register #(.width(32)) register_5 (.D(in_7), .Q(out_21), .clk(in_16));  // open: en, clr
  Register #(.width(32)) register_6 (.D(isRet), .Q(out_22), .clk(in_16));  // open: en, clr
  Control_Packet control_packet_1 (
    .out_10(in_16), .isRet(in_1), .in_9(in_2), .in_1(in_9), .isBgt(isBgt), .isUBranch(isUBranch),
    .isLd(isLd), .isSt(isSt), .in_6(in_14), .in_7(in_15), .out_12(out_24), .out_11(out_23), .out_13(out_25),
    .out_14(out_26), .out_15(out_27), .out_16(out_28), .out_17(out_29), .out_18(out_30), .out_19(out_31));

  // Notes on the sheet:
  //   PC
  //   Branch Target
  //   B
  //   A
  //   OP2
  //   INSTRUCTION
  //   ALU Signals
  //   isBeq
  //   isCall
  //   isWb
endmodule

module EX_MA_Latch (
  input  isCall,
  input  isLd,
  input  isSt,
  input  isWb,
  input  [31:0] in_5,
  input  [31:0] in_6,
  input  [31:0] in_7,
  input  [31:0] in_8,
  input  in_9,
  output [31:0] out_10,
  output [31:0] out_11,
  output [31:0] out_12,
  output [31:0] out_13,
  output out_14,
  output out_15,
  output out_16,
  output out_17
);

  Register #(.width(32)) register_1 (.D(in_5), .Q(out_10));  // open: en, clk, clr
  Register #(.width(32)) register_2 (.D(in_6), .Q(out_11), .clk(in_9));  // open: en, clr
  Register #(.width(32)) register_3 (.D(in_7), .Q(out_12), .clk(in_9));  // open: en, clr
  Register #(.width(32)) register_4 (.D(in_8), .Q(out_13), .clk(in_9));  // open: en, clr
  Register #(.width(1)) register_5 (.D(isLd), .Q(out_14), .clk(in_9));  // open: en, clr
  Register #(.width(1)) register_6 (.D(isSt), .Q(out_15), .clk(in_9));  // open: en, clr
  Register #(.width(1)) register_7 (.D(isCall), .Q(out_16), .clk(in_9));  // open: en, clr
  Register #(.width(1)) register_8 (.D(isWb), .Q(out_17), .clk(in_9));  // open: en, clr

  // Notes on the sheet:
  //   PC
  //   Alu Result
  //   OP2
  //   INSTRUCTION
endmodule

module MA_RW_Latch (
  input  isCall,
  input  isLd,
  input  isWb,
  input  [31:0] in_4,
  input  [31:0] in_5,
  input  [31:0] in_6,
  input  [31:0] in_7,
  input  in_8,
  output [31:0] out_9,
  output [31:0] out_10,
  output [31:0] out_11,
  output [31:0] out_12,
  output out_13,
  output out_14,
  output out_15
);

  Register #(.width(32)) register_1 (.D(in_4), .Q(out_9));  // open: en, clk, clr
  Register #(.width(32)) register_2 (.D(in_5), .Q(out_10), .clk(in_8));  // open: en, clr
  Register #(.width(32)) register_3 (.D(in_6), .Q(out_11), .clk(in_8));  // open: en, clr
  Register #(.width(32)) register_4 (.D(in_7), .Q(out_12), .clk(in_8));  // open: en, clr
  Register #(.width(1)) register_5 (.D(isLd), .Q(out_13), .clk(in_8));  // open: en, clr
  Register #(.width(1)) register_6 (.D(isCall), .Q(out_14), .clk(in_8));  // open: en, clr
  Register #(.width(1)) register_7 (.D(isWb), .Q(out_15), .clk(in_8));  // open: en, clr

  // Notes on the sheet:
  //   PC
  //   LoadResult
  //   Alu Result
  //   INSTRUCTION
endmodule

module Conflict_Detection_Unit_Data_Lock (
  input  [31:0] in_1,
  input  [31:0] in_2,
  output out_3
);

  wire and_1_out, check_opcode_a_1_out_2, check_opcode_b_1_out_2, compare_4_bit_1_out_3,
       compare_4_bit_2_out_3, instruction_split_a_1_hassrc2, or_1_out, or_2_out;
  wire [3:0] instruction_split_a_1_src2, instruction_split_a_1_src_1, instruction_split_b_1_out_3;

  Check_OPcode__A check_opcode_a_1 (.in_1(in_1[31:27]), .out_2(check_opcode_a_1_out_2));
  or or_1 (or_1_out, check_opcode_a_1_out_2, check_opcode_b_1_out_2);
  Instruction_split_A instruction_split_a_1 (
    .in_1(in_1[31:27]), .in_2(in_1[26:0]), .Src_1(instruction_split_a_1_src_1),
    .hasSrc2(instruction_split_a_1_hassrc2), .Src2(instruction_split_a_1_src2));
  Check_OPcode__B check_opcode_b_1 (.in_1(in_2[31:27]), .out_2(check_opcode_b_1_out_2));
  Instruction_split_B instruction_split_b_1 (
    .in_1(in_2[31:27]), .in_2(in_2[26:0]), .out_3(instruction_split_b_1_out_3));
  Compare_4_bit compare_4_bit_1 (
    .in_1(instruction_split_a_1_src_1), .in_2(instruction_split_b_1_out_3), .out_3(compare_4_bit_1_out_3));
  or or_2 (or_2_out, compare_4_bit_1_out_3, and_1_out);
  Multiplexer #(.enable("false")) multiplexer_1 (.in0(or_2_out), .in1(1'b0), .out(out_3), .sel(or_1_out));
  Compare_4_bit compare_4_bit_2 (
    .in_1(instruction_split_a_1_src2), .in_2(instruction_split_b_1_out_3), .out_3(compare_4_bit_2_out_3));
  and and_1 (and_1_out, instruction_split_a_1_hassrc2, compare_4_bit_2_out_3);
endmodule

module Check_OPcode__A (
  input  [4:0] in_1,
  output out_2
);

  wire and_1_out, and_2_out;

  and and_1 (and_1_out, in_1[4], ~in_1[3], ~in_1[2]);  // AND_Gate
  nor nor_1 (out_2, and_1_out, and_2_out);
  and and_2 (and_2_out, ~in_1[4], in_1[3], in_1[2], ~in_1[1], in_1[0]);  // AND_Gate
endmodule

module Check_OPcode__B (
  input  [4:0] in_1,
  output out_2
);

  wire and_1_out, and_2_out, and_3_out, and_4_out, and_5_out;

  and and_1 (and_1_out, ~in_1[4], in_1[2], ~in_1[1], in_1[0]);  // AND_Gate
  and and_2 (and_2_out, ~in_1[4], in_1[3], in_1[2], in_1[0]);  // AND_Gate
  nor nor_1 (out_2, and_1_out, and_2_out, and_3_out, and_4_out, and_5_out);
  and and_3 (and_3_out, in_1[4], ~in_1[3], ~in_1[2], ~in_1[1]);  // AND_Gate
  and and_4 (and_4_out, in_1[4], ~in_1[3], ~in_1[2], ~in_1[0]);  // AND_Gate
  and and_5 (and_5_out, in_1[4], ~in_1[3], ~in_1[1], ~in_1[0]);  // AND_Gate
endmodule

module Instruction_split_A (
  input  [4:0] in_1,
  input  [26:0] in_2,
  output [3:0] Src_1,
  output [3:0] Src2,
  output hasSrc2
);

  wire and_1_out, and_2_out, not_1_out;

  and and_1 (and_1_out, in_1[4], ~in_1[3], in_1[2], ~in_1[1], ~in_1[0]);  // AND_Gate
  and and_2 (and_2_out, ~in_1[4], in_1[3], in_1[2], in_1[1], in_1[0]);  // AND_Gate
  Multiplexer #(.width(4), .enable("false")) multiplexer_1 (
    .in0(in_2[21:18]), .in1(4'b1111), .out(Src_1), .sel(and_1_out));
  not not_1 (not_1_out, in_2[26]);
  Multiplexer #(.enable("false")) multiplexer_2 (.in0(not_1_out), .in1(1'b1), .out(hasSrc2), .sel(and_2_out));
  Multiplexer #(.width(4), .enable("false")) multiplexer_3 (
    .in0(in_2[25:22]), .in1(in_2[17:14]), .out(Src2), .sel(and_2_out));
endmodule

module Instruction_split_B (
  input  [4:0] in_1,
  input  [26:0] in_2,
  output [3:0] out_3
);

  wire and_1_out;

  and and_1 (and_1_out, in_1[4], ~in_1[3], ~in_1[2], in_1[1], in_1[0]);  // AND_Gate
  Multiplexer #(.width(4), .enable("false")) multiplexer_1 (
    .in0(in_2[25:22]), .in1(4'b1111), .out(out_3), .sel(and_1_out));
endmodule

module Compare_4_bit (
  input  [3:0] in_1,
  input  [3:0] in_2,
  output out_3
);

  wire [3:0] not_1_out, subtractor_1_out;

  assign not_1_out = ~in_2;  // NOT_Gate not_1, 4 bits wide
  Subtractor #(.width(4)) subtractor_1 (.a(not_1_out), .b(in_1), .out(subtractor_1_out));  // open: bin, bout
  and and_1 (out_3, subtractor_1_out[3], subtractor_1_out[2], subtractor_1_out[1], subtractor_1_out[0]);
endmodule

module Data_Lock_Unit (
  input  [31:0] in_1,
  input  [31:0] in_2,
  input  [31:0] in_3,
  input  [31:0] in_4,
  output out_5
);

  wire conflict_detection_unit_data_lock_1_out_3, conflict_detection_unit_data_lock_2_out_3,
       conflict_detection_unit_data_lock_3_out_3;

  Conflict_Detection_Unit_Data_Lock conflict_detection_unit_data_lock_1 (
    .in_1(in_1), .in_2(in_2), .out_3(conflict_detection_unit_data_lock_1_out_3));
  Conflict_Detection_Unit_Data_Lock conflict_detection_unit_data_lock_2 (
    .in_1(in_1), .in_2(in_3), .out_3(conflict_detection_unit_data_lock_2_out_3));
  or or_1 (out_5, conflict_detection_unit_data_lock_1_out_3, conflict_detection_unit_data_lock_2_out_3, conflict_detection_unit_data_lock_3_out_3);
  Conflict_Detection_Unit_Data_Lock conflict_detection_unit_data_lock_3 (
    .in_1(in_1), .in_2(in_4), .out_3(conflict_detection_unit_data_lock_3_out_3));
endmodule

module Conflict_Detection_Unit__Forwarding_FO (
  input  [31:0] in_1,
  input  [31:0] in_2,
  output out_3
);

  wire and_1_out, check_opcode_a_1_out_2, check_opcode_b_1_out_2, compare_4_bit_1_out_3,
       compare_4_bit_2_out_3, instruction_split_a_1_hassrc2, or_1_out, or_2_out;
  wire [3:0] instruction_split_a_1_src2, instruction_split_a_1_src_1, instruction_split_b_1_out_3;

  Check_OPcode__A check_opcode_a_1 (.in_1(in_1[31:27]), .out_2(check_opcode_a_1_out_2));
  or or_1 (or_1_out, check_opcode_a_1_out_2, check_opcode_b_1_out_2);
  Instruction_split_A instruction_split_a_1 (
    .in_1(in_1[31:27]), .in_2(in_1[26:0]), .Src_1(instruction_split_a_1_src_1),
    .hasSrc2(instruction_split_a_1_hassrc2), .Src2(instruction_split_a_1_src2));
  Check_OPcode__B check_opcode_b_1 (.in_1(in_2[31:27]), .out_2(check_opcode_b_1_out_2));
  Instruction_split_B instruction_split_b_1 (
    .in_1(in_2[31:27]), .in_2(in_2[26:0]), .out_3(instruction_split_b_1_out_3));
  Compare_4_bit compare_4_bit_1 (
    .in_1(instruction_split_a_1_src_1), .in_2(instruction_split_b_1_out_3), .out_3(compare_4_bit_1_out_3));
  or or_2 (or_2_out, compare_4_bit_1_out_3, and_1_out);
  Multiplexer #(.enable("false")) multiplexer_1 (.in0(or_2_out), .in1(1'b0), .out(out_3), .sel(or_1_out));
  Compare_4_bit compare_4_bit_2 (
    .in_1(instruction_split_a_1_src2), .in_2(instruction_split_b_1_out_3), .out_3(compare_4_bit_2_out_3));
  and and_1 (and_1_out, instruction_split_a_1_hassrc2, compare_4_bit_2_out_3);
endmodule

module Instruction_split_A__Forwarding (
  input  [4:0] in_1,
  input  [26:0] in_2,
  output [3:0] Src_1,
  output [3:0] Src2,
  output hasSrc2
);

  wire and_1_out, and_2_out;

  and and_1 (and_1_out, in_1[4], ~in_1[3], in_1[2], ~in_1[1], ~in_1[0]);  // AND_Gate
  and and_2 (and_2_out, ~in_1[4], in_1[3], in_1[2], in_1[1], in_1[0]);  // AND_Gate
  Multiplexer #(.width(4), .enable("false")) multiplexer_1 (
    .in0(in_2[21:18]), .in1(4'b1111), .out(Src_1), .sel(and_1_out));
  Multiplexer #(.enable("false")) multiplexer_2 (.in0(in_2[26]), .in1(1'b1), .out(hasSrc2), .sel(and_2_out));
  Multiplexer #(.width(4), .enable("false")) multiplexer_3 (
    .in0(in_2[25:22]), .in1(in_2[17:14]), .out(Src2), .sel(and_2_out));
endmodule

module Conflict_Detection_Unit__Forwarding_SO (
  input  [31:0] in_1,
  input  [31:0] in_2,
  output out_3
);

  wire and_1_out, check_opcode_a_1_out_2, check_opcode_b_1_out_2, compare_4_bit_1_out_3,
       compare_4_bit_2_out_3, instruction_split_a_1_hassrc2, or_1_out, or_2_out;
  wire [3:0] instruction_split_a_1_src2, instruction_split_a_1_src_1, instruction_split_b_1_out_3;

  Check_OPcode__A check_opcode_a_1 (.in_1(in_1[31:27]), .out_2(check_opcode_a_1_out_2));
  or or_1 (or_1_out, check_opcode_a_1_out_2, check_opcode_b_1_out_2);
  Instruction_split_A instruction_split_a_1 (
    .in_1(in_1[31:27]), .in_2(in_1[26:0]), .Src_1(instruction_split_a_1_src_1),
    .hasSrc2(instruction_split_a_1_hassrc2), .Src2(instruction_split_a_1_src2));
  Check_OPcode__B check_opcode_b_1 (.in_1(in_2[31:27]), .out_2(check_opcode_b_1_out_2));
  Instruction_split_B instruction_split_b_1 (
    .in_1(in_2[31:27]), .in_2(in_2[26:0]), .out_3(instruction_split_b_1_out_3));
  Compare_4_bit compare_4_bit_1 (
    .in_1(instruction_split_a_1_src_1), .in_2(instruction_split_b_1_out_3), .out_3(compare_4_bit_1_out_3));
  or or_2 (or_2_out, compare_4_bit_1_out_3, and_1_out);
  Multiplexer #(.enable("false")) multiplexer_1 (.in0(or_2_out), .in1(1'b0), .out(out_3), .sel(or_1_out));
  Compare_4_bit compare_4_bit_2 (
    .in_1(instruction_split_a_1_src2), .in_2(instruction_split_b_1_out_3), .out_3(compare_4_bit_2_out_3));
  and and_1 (and_1_out, instruction_split_a_1_hassrc2, compare_4_bit_2_out_3);
endmodule

module Control_Packet (
  input  in_1,
  input  isBgt,
  input  isUBranch,
  input  isLd,
  input  isSt,
  input  in_6,
  input  in_7,
  input  isRet,
  input  [12:0] in_9,
  output out_10,
  output [12:0] out_11,
  output out_12,
  output out_13,
  output out_14,
  output out_15,
  output out_16,
  output out_17,
  output out_18,
  output out_19
);

  Register #(.width(1)) register_1 (.D(isRet), .Q(out_12), .clk(out_10));  // open: en, clr
  Register #(.width(13)) register_2 (.D(in_9), .Q(out_11), .clk(out_10));  // open: en, clr
  Register #(.width(1)) register_3 (.D(in_1), .Q(out_13), .clk(out_10));  // open: en, clr
  Register #(.width(1)) register_4 (.D(isBgt), .Q(out_14), .clk(out_10));  // open: en, clr
  Register #(.width(1)) register_5 (.D(isUBranch), .Q(out_15), .clk(out_10));  // open: en, clr
  Register #(.width(1)) register_6 (.D(isLd), .Q(out_16), .clk(out_10));  // open: en, clr
  Register #(.width(1)) register_7 (.D(isSt), .Q(out_17), .clk(out_10));  // open: en, clr
  Register #(.width(1)) register_8 (.D(in_6), .Q(out_18), .clk(out_10));  // open: en, clr
  Register #(.width(1)) register_9 (.D(in_7), .Q(out_19), .clk(out_10));  // open: en, clr

  // Notes on the sheet:
  //   ALU Signals
  //   isBeq
  //   isCall
  //   isWb
endmodule
